// Logisim project logisim-trinary-simulator.circ as structural Verilog: 28 circuits, main circuit Introduction and how trinary is modeled
module Introduction_and_how_trinary_is_modeled (
  input  [1:0] in_1,
  output out_2,
  output out_3,
  output out_4
);

  wire decoder_1_out0, decoder_1_out3, tri_led_driver_1_out_2, tri_led_driver_1_out_3, tri_led_driver_1_out_4;

  LED led_1 (.in(tri_led_driver_1_out_2));
  LED led_2 (.in(tri_led_driver_1_out_4));
  tri_led_driver tri_led_driver_1 (
    .in_1(in_1), .out_2(tri_led_driver_1_out_2), .out_3(tri_led_driver_1_out_3),
    .out_4(tri_led_driver_1_out_4));
  LED led_3 (.in(tri_led_driver_1_out_3));
  Decoder #(.select(2)) decoder_1 (
    .out0(decoder_1_out0), .out1(out_2), .out2(out_4), .out3(decoder_1_out3), .sel(in_1));
  or or_1 (out_3, decoder_1_out0, decoder_1_out3);

  // Notes on the sheet:
  //   This is *NOT* a valid (simulated) trinary circut.
  //   Its outputs are not (simulated) tri-level.
  //   It is usefull for building (simulations of) trinary circuits
  //   Although the *wires* are simulations, the
  //   gates are 'real' trinary gates.  If we could replace the
  //   split/joins with weird D/A circuits, it would be all real.
  //   Look at "TNAND fast" to see how the gates should be implemented in real hardware.
  //   This is all copyrighted, and licensed to you if you desire, under GPL 3 or later.
  //   Simple system for simulating trinary logic circuits.
  //   The usual sort of implementation is used here,
  //   we simulate a single wire with 3 level signals
  //    with a pair of wires carying two level signals.
  //   The high bit (Logisim is little endian, it is numbered 1) represents -1 often notated j
  //   The value 11 is considered non-standard, many circuits will treat it as 00 though.
  //   00 is used to represent 0 often notated o
  //   The low bit (numbered 0) represents +1 always notated 1
  //   Representation of +1 is on the pair of wires
  //   +1 asserted high
  //   0 asserted high
  //   -1 asserted high
endmodule

module Sampler__copy_LEDs_from_here (
  input  in_1
);

  wire _0_out, _1_out, _2_out, _3_out, _4_out, A_out, B_out, C_out, D_out, n2t_to_7seg_driver_1_out_2,
       n2t_to_7seg_driver_1_out_3, n2t_to_7seg_driver_1_out_4, n2t_to_7seg_driver_1_out_5,
       n2t_to_7seg_driver_1_out_6, n2t_to_7seg_driver_1_out_7, n2t_to_7seg_driver_1_out_8,
       n2t_to_7seg_driver_1_out_9, n2t_to_7seg_driver_2_out_2, n2t_to_7seg_driver_2_out_3,
       n2t_to_7seg_driver_2_out_4, n2t_to_7seg_driver_2_out_5, n2t_to_7seg_driver_2_out_6,
       n2t_to_7seg_driver_2_out_7, n2t_to_7seg_driver_2_out_8, n2t_to_7seg_driver_2_out_9,
       n2t_to_7seg_driver_3_out_2, n2t_to_7seg_driver_3_out_3, n2t_to_7seg_driver_3_out_4,
       n2t_to_7seg_driver_3_out_5, n2t_to_7seg_driver_3_out_6, n2t_to_7seg_driver_3_out_7,
       n2t_to_7seg_driver_3_out_8, n2t_to_7seg_driver_3_out_9, n2t_to_7seg_driver_4_out_2,
       n2t_to_7seg_driver_4_out_3, n2t_to_7seg_driver_4_out_4, n2t_to_7seg_driver_4_out_5,
       n2t_to_7seg_driver_4_out_6, n2t_to_7seg_driver_4_out_7, n2t_to_7seg_driver_4_out_8,
       n2t_to_7seg_driver_4_out_9, n2t_to_7seg_driver_5_out_2, n2t_to_7seg_driver_5_out_3,
       n2t_to_7seg_driver_5_out_4, n2t_to_7seg_driver_5_out_5, n2t_to_7seg_driver_5_out_6,
       n2t_to_7seg_driver_5_out_7, n2t_to_7seg_driver_5_out_8, n2t_to_7seg_driver_5_out_9,
       n2t_to_7seg_driver_6_out_2, n2t_to_7seg_driver_6_out_3, n2t_to_7seg_driver_6_out_4,
       n2t_to_7seg_driver_6_out_5, n2t_to_7seg_driver_6_out_6, n2t_to_7seg_driver_6_out_7,
       n2t_to_7seg_driver_6_out_8, n2t_to_7seg_driver_6_out_9, tri_led_driver_1_out_2,
       tri_led_driver_1_out_3, tri_led_driver_1_out_4, tri_led_driver_2_out_2, tri_led_driver_2_out_3,
       tri_led_driver_2_out_4, tri_led_driver_3_out_2, tri_led_driver_3_out_3, tri_led_driver_3_out_4,
       tri_led_driver_4_out_2, tri_led_driver_4_out_3, tri_led_driver_4_out_4, tri_led_driver_5_out_2,
       tri_led_driver_5_out_3, tri_led_driver_5_out_4, tri_led_driver_6_out_2, tri_led_driver_6_out_3,
       tri_led_driver_6_out_4, tri_led_driver_7_out_2, tri_led_driver_7_out_3, tri_led_driver_7_out_4,
       tri_led_driver_8_out_2, tri_led_driver_8_out_3, tri_led_driver_8_out_4, tri_led_driver_9_out_2,
       tri_led_driver_9_out_3, tri_led_driver_9_out_4, tri_led_driver_10_out_2, tri_led_driver_10_out_3,
       tri_led_driver_10_out_4, tri_led_driver_11_out_2, tri_led_driver_11_out_3, tri_led_driver_11_out_4,
       tri_led_driver_12_out_2, tri_led_driver_12_out_3, tri_led_driver_12_out_4, tri_led_driver_13_out_2,
       tri_led_driver_13_out_3, tri_led_driver_13_out_4, tri_led_driver_14_out_2, tri_led_driver_14_out_3,
       tri_led_driver_14_out_4, tri_led_driver_15_out_2, tri_led_driver_15_out_3, tri_led_driver_15_out_4,
       tri_led_driver_16_out_2, tri_led_driver_16_out_3, tri_led_driver_16_out_4, tri_led_driver_17_out_2,
       tri_led_driver_17_out_3, tri_led_driver_17_out_4, tri_led_driver_18_out_2, tri_led_driver_18_out_3,
       tri_led_driver_18_out_4, tri_led_driver_19_out_2, tri_led_driver_19_out_3, tri_led_driver_19_out_4,
       tri_led_driver_20_out_2, tri_led_driver_20_out_3, tri_led_driver_20_out_4, tri_led_driver_21_out_2,
       tri_led_driver_21_out_3, tri_led_driver_21_out_4, tri_led_driver_22_out_2, tri_led_driver_22_out_3,
       tri_led_driver_22_out_4, tri_led_driver_23_out_2, tri_led_driver_23_out_3, tri_led_driver_23_out_4,
       tri_led_driver_24_out_2, tri_led_driver_24_out_3, tri_led_driver_24_out_4, tri_led_driver_25_out_2,
       tri_led_driver_25_out_3, tri_led_driver_25_out_4, tri_led_driver_26_out_2, tri_led_driver_26_out_3,
       tri_led_driver_26_out_4, tri_led_driver_27_out_2, tri_led_driver_27_out_3, tri_led_driver_27_out_4,
       tri_led_driver_28_out_2, tri_led_driver_28_out_3, tri_led_driver_28_out_4;
  wire [0:0] button_1_out, clock_1_out;
  wire [1:0] cd_cycle_down_1_jo1____1jo, cu_cycle_up_1_jo1____o1j, d_latch_level_triggered_1_q,
       nti_negative_trinary_inverter_1_jo1____11j, pti_positive_trinary_inverter_1_jo1____1jj,
       register_master_slave_d_latch_1_q, sti_simple_ternary_inverter_1_jo1____1oj,
       sti_simple_ternary_inverter_2_jo1____1oj, sti_simple_ternary_inverter_3_jo1____1oj,
       tnand_3_input_1_out_4, tnand_3_input_2_out_4, tnor_3_input_1_out_4, tnor_3_input_2_out_4;
  wire [11:0] keyboard_input_1_out_10, n6t_counter_1_out_3;

  Button _2 (.out(_2_out));
  Button A (.out(A_out));
  Button D (.out(D_out));
  Button button_1 (.out(button_1_out[0]));
  _7_Segment_Display u_7_segment_display_1 ();  // open: g, f, a, b, e, d, c, dp
  keyboard_input keyboard_input_1 (
    .in_1(_2_out), .in_2(_3_out), .in_3(_4_out), .in_4(A_out), .in_5(_0_out), .in_6(_1_out), .in_7(D_out),
    .in_8(C_out), .in_9(B_out), .out_10(keyboard_input_1_out_10));
  Button _3 (.out(_3_out));
  Button _4 (.out(_4_out));
  Button _1 (.out(_1_out));
  Button _0 (.out(_0_out));
  Button B (.out(B_out));
  Button C (.out(C_out));
  _7_Segment_Display u_7_segment_display_2 (
    .g(n2t_to_7seg_driver_2_out_3), .f(n2t_to_7seg_driver_2_out_4), .a(n2t_to_7seg_driver_2_out_9),
    .b(n2t_to_7seg_driver_2_out_8), .e(n2t_to_7seg_driver_2_out_5), .d(n2t_to_7seg_driver_2_out_6),
    .c(n2t_to_7seg_driver_2_out_7), .dp(n2t_to_7seg_driver_2_out_2));
  _7_Segment_Display u_7_segment_display_3 (
    .g(n2t_to_7seg_driver_1_out_3), .f(n2t_to_7seg_driver_1_out_4), .a(n2t_to_7seg_driver_1_out_9),
    .b(n2t_to_7seg_driver_1_out_8), .e(n2t_to_7seg_driver_1_out_5), .d(n2t_to_7seg_driver_1_out_6),
    .c(n2t_to_7seg_driver_1_out_7), .dp(n2t_to_7seg_driver_1_out_2));
  _2t_to_7seg_driver u_2t_to_7seg_driver_1 (
    .in_1(keyboard_input_1_out_10[11:8]), .out_2(n2t_to_7seg_driver_1_out_2),
    .out_3(n2t_to_7seg_driver_1_out_3), .out_4(n2t_to_7seg_driver_1_out_4),
    .out_5(n2t_to_7seg_driver_1_out_5), .out_6(n2t_to_7seg_driver_1_out_6),
    .out_7(n2t_to_7seg_driver_1_out_7), .out_8(n2t_to_7seg_driver_1_out_8), .out_9(n2t_to_7seg_driver_1_out_9));
  LED led_1 (.in(tri_led_driver_2_out_2));
  LED led_2 (.in(tri_led_driver_1_out_2));
  LED led_3 (.in(tri_led_driver_4_out_2));
  LED led_4 (.in(tri_led_driver_2_out_3));
  LED led_5 (.in(tri_led_driver_1_out_3));
  tri_led_driver tri_led_driver_1 (
    .in_1(keyboard_input_1_out_10[11:10]), .out_2(tri_led_driver_1_out_2), .out_3(tri_led_driver_1_out_3),
    .out_4(tri_led_driver_1_out_4));
  tri_led_driver tri_led_driver_2 (
    .in_1(keyboard_input_1_out_10[9:8]), .out_2(tri_led_driver_2_out_2), .out_3(tri_led_driver_2_out_3),
    .out_4(tri_led_driver_2_out_4));
  LED led_6 (.in(tri_led_driver_2_out_4));
  LED led_7 (.in(tri_led_driver_4_out_4));
  LED led_8 (.in(tri_led_driver_1_out_4));
  Clock clock_1 (.out(clock_1_out[0]));
  LED led_9 (.in(tri_led_driver_3_out_2));
  tri_led_driver tri_led_driver_3 (
    .in_1(d_latch_level_triggered_1_q), .out_2(tri_led_driver_3_out_2), .out_3(tri_led_driver_3_out_3),
    .out_4(tri_led_driver_3_out_4));
  LED led_10 (.in(tri_led_driver_3_out_3));
  D_Latch__level_triggered d_latch_level_triggered_1 (
    .D(keyboard_input_1_out_10[1:0]), .E_1({1'b0, button_1_out[0]}), .Q(d_latch_level_triggered_1_q));
  LED led_11 (.in(tri_led_driver_3_out_4));
  _7_Segment_Display u_7_segment_display_4 (
    .g(n2t_to_7seg_driver_3_out_3), .f(n2t_to_7seg_driver_3_out_4), .a(n2t_to_7seg_driver_3_out_9),
    .b(n2t_to_7seg_driver_3_out_8), .e(n2t_to_7seg_driver_3_out_5), .d(n2t_to_7seg_driver_3_out_6),
    .c(n2t_to_7seg_driver_3_out_7), .dp(n2t_to_7seg_driver_3_out_2));
  _2t_to_7seg_driver u_2t_to_7seg_driver_2 (
    .in_1(keyboard_input_1_out_10[7:4]), .out_2(n2t_to_7seg_driver_2_out_2),
    .out_3(n2t_to_7seg_driver_2_out_3), .out_4(n2t_to_7seg_driver_2_out_4),
    .out_5(n2t_to_7seg_driver_2_out_5), .out_6(n2t_to_7seg_driver_2_out_6),
    .out_7(n2t_to_7seg_driver_2_out_7), .out_8(n2t_to_7seg_driver_2_out_8), .out_9(n2t_to_7seg_driver_2_out_9));
  LED led_12 (.in(tri_led_driver_6_out_2));
  LED led_13 (.in(tri_led_driver_5_out_2));
  tri_led_driver tri_led_driver_4 (
    .in_1(keyboard_input_1_out_10[7:6]), .out_2(tri_led_driver_4_out_2), .out_3(tri_led_driver_4_out_3),
    .out_4(tri_led_driver_4_out_4));
  LED led_14 (.in(tri_led_driver_6_out_3));
  tri_led_driver tri_led_driver_5 (
    .in_1(keyboard_input_1_out_10[5:4]), .out_2(tri_led_driver_5_out_2), .out_3(tri_led_driver_5_out_3),
    .out_4(tri_led_driver_5_out_4));
  LED led_15 (.in(tri_led_driver_5_out_3));
  tri_led_driver tri_led_driver_6 (
    .in_1(keyboard_input_1_out_10[3:2]), .out_2(tri_led_driver_6_out_2), .out_3(tri_led_driver_6_out_3),
    .out_4(tri_led_driver_6_out_4));
  LED led_16 (.in(tri_led_driver_4_out_3));
  LED led_17 (.in(tri_led_driver_6_out_4));
  LED led_18 (.in(tri_led_driver_5_out_4));
  _6t_counter u_6t_counter_1 (.in_1({1'b0, clock_1_out[0]}), .in_2({1'b0, in_1}), .out_3(n6t_counter_1_out_3));
  Register__master_slave_D_latch register_master_slave_d_latch_1 (
    .D(keyboard_input_1_out_10[1:0]),
    .Clock__pulse__latch_in_on_rising_edge__out_on_falling({1'b0, button_1_out[0]}),
    .Q(register_master_slave_d_latch_1_q));
  _2t_to_7seg_driver u_2t_to_7seg_driver_3 (
    .in_1(keyboard_input_1_out_10[3:0]), .out_2(n2t_to_7seg_driver_3_out_2),
    .out_3(n2t_to_7seg_driver_3_out_3), .out_4(n2t_to_7seg_driver_3_out_4),
    .out_5(n2t_to_7seg_driver_3_out_5), .out_6(n2t_to_7seg_driver_3_out_6),
    .out_7(n2t_to_7seg_driver_3_out_7), .out_8(n2t_to_7seg_driver_3_out_8), .out_9(n2t_to_7seg_driver_3_out_9));
  LED led_19 (.in(tri_led_driver_7_out_2));
  LED led_20 (.in(tri_led_driver_7_out_3));
  tri_led_driver tri_led_driver_7 (
    .in_1(keyboard_input_1_out_10[1:0]), .out_2(tri_led_driver_7_out_2), .out_3(tri_led_driver_7_out_3),
    .out_4(tri_led_driver_7_out_4));
  LED led_21 (.in(tri_led_driver_7_out_4));
  LED led_22 (.in(tri_led_driver_8_out_2));
  LED led_23 (.in(tri_led_driver_8_out_3));
  tri_led_driver tri_led_driver_8 (
    .in_1(keyboard_input_1_out_10[5:4]), .out_2(tri_led_driver_8_out_2), .out_3(tri_led_driver_8_out_3),
    .out_4(tri_led_driver_8_out_4));
  LED led_24 (.in(tri_led_driver_8_out_4));
  LED led_25 (.in(tri_led_driver_9_out_2));
  tri_led_driver tri_led_driver_9 (
    .in_1(register_master_slave_d_latch_1_q), .out_2(tri_led_driver_9_out_2), .out_3(tri_led_driver_9_out_3),
    .out_4(tri_led_driver_9_out_4));
  LED led_26 (.in(tri_led_driver_9_out_3));
  LED led_27 (.in(tri_led_driver_9_out_4));
  _7_Segment_Display u_7_segment_display_5 (
    .g(n2t_to_7seg_driver_4_out_3), .f(n2t_to_7seg_driver_4_out_4), .a(n2t_to_7seg_driver_4_out_9),
    .b(n2t_to_7seg_driver_4_out_8), .e(n2t_to_7seg_driver_4_out_5), .d(n2t_to_7seg_driver_4_out_6),
    .c(n2t_to_7seg_driver_4_out_7), .dp(n2t_to_7seg_driver_4_out_2));
  _7_Segment_Display u_7_segment_display_6 (
    .g(n2t_to_7seg_driver_5_out_3), .f(n2t_to_7seg_driver_5_out_4), .a(n2t_to_7seg_driver_5_out_9),
    .b(n2t_to_7seg_driver_5_out_8), .e(n2t_to_7seg_driver_5_out_5), .d(n2t_to_7seg_driver_5_out_6),
    .c(n2t_to_7seg_driver_5_out_7), .dp(n2t_to_7seg_driver_5_out_2));
  _2t_to_7seg_driver u_2t_to_7seg_driver_4 (
    .in_1(n6t_counter_1_out_3[11:8]), .out_2(n2t_to_7seg_driver_4_out_2), .out_3(n2t_to_7seg_driver_4_out_3),
    .out_4(n2t_to_7seg_driver_4_out_4), .out_5(n2t_to_7seg_driver_4_out_5),
    .out_6(n2t_to_7seg_driver_4_out_6), .out_7(n2t_to_7seg_driver_4_out_7),
    .out_8(n2t_to_7seg_driver_4_out_8), .out_9(n2t_to_7seg_driver_4_out_9));
  LED led_28 (.in(tri_led_driver_11_out_2));
  LED led_29 (.in(tri_led_driver_10_out_2));
  LED led_30 (.in(tri_led_driver_12_out_2));
  tri_led_driver tri_led_driver_10 (
    .in_1(n6t_counter_1_out_3[9:8]), .out_2(tri_led_driver_10_out_2), .out_3(tri_led_driver_10_out_3),
    .out_4(tri_led_driver_10_out_4));
  LED led_31 (.in(tri_led_driver_11_out_3));
  LED led_32 (.in(tri_led_driver_12_out_3));
  tri_led_driver tri_led_driver_11 (
    .in_1(n6t_counter_1_out_3[7:6]), .out_2(tri_led_driver_11_out_2), .out_3(tri_led_driver_11_out_3),
    .out_4(tri_led_driver_11_out_4));
  tri_led_driver tri_led_driver_12 (
    .in_1(n6t_counter_1_out_3[11:10]), .out_2(tri_led_driver_12_out_2), .out_3(tri_led_driver_12_out_3),
    .out_4(tri_led_driver_12_out_4));
  LED led_33 (.in(tri_led_driver_10_out_3));
  LED led_34 (.in(tri_led_driver_12_out_4));
  LED led_35 (.in(tri_led_driver_10_out_4));
  LED led_36 (.in(tri_led_driver_11_out_4));
  LED led_37 (.in(tri_led_driver_13_out_2));
  tri_led_driver tri_led_driver_13 (
    .in_1(keyboard_input_1_out_10[1:0]), .out_2(tri_led_driver_13_out_2), .out_3(tri_led_driver_13_out_3),
    .out_4(tri_led_driver_13_out_4));
  LED led_38 (.in(tri_led_driver_13_out_3));
  LED led_39 (.in(tri_led_driver_13_out_4));
  _7_Segment_Display u_7_segment_display_7 (
    .g(n2t_to_7seg_driver_6_out_3), .f(n2t_to_7seg_driver_6_out_4), .a(n2t_to_7seg_driver_6_out_9),
    .b(n2t_to_7seg_driver_6_out_8), .e(n2t_to_7seg_driver_6_out_5), .d(n2t_to_7seg_driver_6_out_6),
    .c(n2t_to_7seg_driver_6_out_7), .dp(n2t_to_7seg_driver_6_out_2));
  _2t_to_7seg_driver u_2t_to_7seg_driver_5 (
    .in_1(n6t_counter_1_out_3[7:4]), .out_2(n2t_to_7seg_driver_5_out_2), .out_3(n2t_to_7seg_driver_5_out_3),
    .out_4(n2t_to_7seg_driver_5_out_4), .out_5(n2t_to_7seg_driver_5_out_5),
    .out_6(n2t_to_7seg_driver_5_out_6), .out_7(n2t_to_7seg_driver_5_out_7),
    .out_8(n2t_to_7seg_driver_5_out_8), .out_9(n2t_to_7seg_driver_5_out_9));
  _2t_to_7seg_driver u_2t_to_7seg_driver_6 (
    .in_1(n6t_counter_1_out_3[3:0]), .out_2(n2t_to_7seg_driver_6_out_2), .out_3(n2t_to_7seg_driver_6_out_3),
    .out_4(n2t_to_7seg_driver_6_out_4), .out_5(n2t_to_7seg_driver_6_out_5),
    .out_6(n2t_to_7seg_driver_6_out_6), .out_7(n2t_to_7seg_driver_6_out_7),
    .out_8(n2t_to_7seg_driver_6_out_8), .out_9(n2t_to_7seg_driver_6_out_9));
  LED led_40 (.in(tri_led_driver_15_out_2));
  LED led_41 (.in(tri_led_driver_16_out_2));
  LED led_42 (.in(tri_led_driver_14_out_2));
  tri_led_driver tri_led_driver_14 (
    .in_1(n6t_counter_1_out_3[3:2]), .out_2(tri_led_driver_14_out_2), .out_3(tri_led_driver_14_out_3),
    .out_4(tri_led_driver_14_out_4));
  LED led_43 (.in(tri_led_driver_15_out_3));
  LED led_44 (.in(tri_led_driver_14_out_3));
  tri_led_driver tri_led_driver_15 (
    .in_1(n6t_counter_1_out_3[5:4]), .out_2(tri_led_driver_15_out_2), .out_3(tri_led_driver_15_out_3),
    .out_4(tri_led_driver_15_out_4));
  LED led_45 (.in(tri_led_driver_16_out_4));
  LED led_46 (.in(tri_led_driver_15_out_4));
  LED led_47 (.in(tri_led_driver_14_out_4));
  CU_Cycle_Up cu_cycle_up_1 (.in_1(keyboard_input_1_out_10[1:0]), .jo1____o1j(cu_cycle_up_1_jo1____o1j));
  CD_Cycle_Down cd_cycle_down_1 (.in_1(keyboard_input_1_out_10[1:0]), .jo1____1jo(cd_cycle_down_1_jo1____1jo));
  TNAND_3_input tnand_3_input_1 (
    .in_1(keyboard_input_1_out_10[1:0]), .in_2(keyboard_input_1_out_10[1:0]),
    .in_3(keyboard_input_1_out_10[1:0]), .out_4(tnand_3_input_1_out_4));
  TNOR_3_input tnor_3_input_1 (
    .in_1(keyboard_input_1_out_10[1:0]), .in_2(keyboard_input_1_out_10[1:0]),
    .in_3(keyboard_input_1_out_10[1:0]), .out_4(tnor_3_input_1_out_4));
  TNOR_3_input tnor_3_input_2 (
    .in_1(keyboard_input_1_out_10[1:0]), .in_2(keyboard_input_1_out_10[1:0]),
    .in_3(keyboard_input_1_out_10[5:4]), .out_4(tnor_3_input_2_out_4));
  TNAND_3_input tnand_3_input_2 (
    .in_1(keyboard_input_1_out_10[1:0]), .in_2(keyboard_input_1_out_10[1:0]),
    .in_3(keyboard_input_1_out_10[5:4]), .out_4(tnand_3_input_2_out_4));
  tri_led_driver tri_led_driver_16 (
    .in_1(n6t_counter_1_out_3[1:0]), .out_2(tri_led_driver_16_out_2), .out_3(tri_led_driver_16_out_3),
    .out_4(tri_led_driver_16_out_4));
  LED led_48 (.in(tri_led_driver_16_out_3));
  LED led_49 (.in(tri_led_driver_17_out_2));
  LED led_50 (.in(tri_led_driver_17_out_3));
  tri_led_driver tri_led_driver_17 (
    .in_1(cu_cycle_up_1_jo1____o1j), .out_2(tri_led_driver_17_out_2), .out_3(tri_led_driver_17_out_3),
    .out_4(tri_led_driver_17_out_4));
  LED led_51 (.in(tri_led_driver_17_out_4));
  LED led_52 (.in(tri_led_driver_18_out_2));
  LED led_53 (.in(tri_led_driver_18_out_3));
  tri_led_driver tri_led_driver_18 (
    .in_1(cd_cycle_down_1_jo1____1jo), .out_2(tri_led_driver_18_out_2), .out_3(tri_led_driver_18_out_3),
    .out_4(tri_led_driver_18_out_4));
  LED led_54 (.in(tri_led_driver_18_out_4));
  LED led_55 (.in(tri_led_driver_19_out_2));
  tri_led_driver tri_led_driver_19 (
    .in_1(tnand_3_input_1_out_4), .out_2(tri_led_driver_19_out_2), .out_3(tri_led_driver_19_out_3),
    .out_4(tri_led_driver_19_out_4));
  LED led_56 (.in(tri_led_driver_19_out_3));
  LED led_57 (.in(tri_led_driver_19_out_4));
  LED led_58 (.in(tri_led_driver_20_out_2));
  LED led_59 (.in(tri_led_driver_20_out_3));
  tri_led_driver tri_led_driver_20 (
    .in_1(tnor_3_input_1_out_4), .out_2(tri_led_driver_20_out_2), .out_3(tri_led_driver_20_out_3),
    .out_4(tri_led_driver_20_out_4));
  LED led_60 (.in(tri_led_driver_20_out_4));
  LED led_61 (.in(tri_led_driver_21_out_2));
  tri_led_driver tri_led_driver_21 (
    .in_1(tnor_3_input_2_out_4), .out_2(tri_led_driver_21_out_2), .out_3(tri_led_driver_21_out_3),
    .out_4(tri_led_driver_21_out_4));
  LED led_62 (.in(tri_led_driver_21_out_3));
  LED led_63 (.in(tri_led_driver_21_out_4));
  LED led_64 (.in(tri_led_driver_22_out_2));
  tri_led_driver tri_led_driver_22 (
    .in_1(tnand_3_input_2_out_4), .out_2(tri_led_driver_22_out_2), .out_3(tri_led_driver_22_out_3),
    .out_4(tri_led_driver_22_out_4));
  LED led_65 (.in(tri_led_driver_22_out_3));
  LED led_66 (.in(tri_led_driver_22_out_4));
  NTI_Negative_Trinary_Inverter nti_negative_trinary_inverter_1 (
    .in_1(keyboard_input_1_out_10[1:0]), .jo1____11j(nti_negative_trinary_inverter_1_jo1____11j));
  STI_Simple_Ternary_Inverter sti_simple_ternary_inverter_1 (
    .in_1(keyboard_input_1_out_10[1:0]), .jo1____1oj(sti_simple_ternary_inverter_1_jo1____1oj));
  PTI_Positive_Trinary_Inverter pti_positive_trinary_inverter_1 (
    .in_1(keyboard_input_1_out_10[1:0]), .jo1____1jj(pti_positive_trinary_inverter_1_jo1____1jj));
  STI_Simple_Ternary_Inverter sti_simple_ternary_inverter_2 (
    .in_1(tnor_3_input_2_out_4), .jo1____1oj(sti_simple_ternary_inverter_2_jo1____1oj));
  STI_Simple_Ternary_Inverter sti_simple_ternary_inverter_3 (
    .in_1(tnand_3_input_2_out_4), .jo1____1oj(sti_simple_ternary_inverter_3_jo1____1oj));
  LED led_67 (.in(tri_led_driver_23_out_2));
  LED led_68 (.in(tri_led_driver_23_out_3));
  tri_led_driver tri_led_driver_23 (
    .in_1(keyboard_input_1_out_10[1:0]), .out_2(tri_led_driver_23_out_2), .out_3(tri_led_driver_23_out_3),
    .out_4(tri_led_driver_23_out_4));
  LED led_69 (.in(tri_led_driver_23_out_4));
  LED led_70 (.in(tri_led_driver_24_out_2));
  tri_led_driver tri_led_driver_24 (
    .in_1(nti_negative_trinary_inverter_1_jo1____11j), .out_2(tri_led_driver_24_out_2),
    .out_3(tri_led_driver_24_out_3), .out_4(tri_led_driver_24_out_4));
  LED led_71 (.in(tri_led_driver_24_out_3));
  LED led_72 (.in(tri_led_driver_24_out_4));
  LED led_73 (.in(tri_led_driver_25_out_2));
  LED led_74 (.in(tri_led_driver_25_out_3));
  tri_led_driver tri_led_driver_25 (
    .in_1(sti_simple_ternary_inverter_1_jo1____1oj), .out_2(tri_led_driver_25_out_2),
    .out_3(tri_led_driver_25_out_3), .out_4(tri_led_driver_25_out_4));
  LED led_75 (.in(tri_led_driver_25_out_4));
  LED led_76 (.in(tri_led_driver_26_out_2));
  LED led_77 (.in(tri_led_driver_26_out_3));
  tri_led_driver tri_led_driver_26 (
    .in_1(pti_positive_trinary_inverter_1_jo1____1jj), .out_2(tri_led_driver_26_out_2),
    .out_3(tri_led_driver_26_out_3), .out_4(tri_led_driver_26_out_4));
  LED led_78 (.in(tri_led_driver_26_out_4));
  LED led_79 (.in(tri_led_driver_27_out_2));
  LED led_80 (.in(tri_led_driver_27_out_3));
  tri_led_driver tri_led_driver_27 (
    .in_1(sti_simple_ternary_inverter_2_jo1____1oj), .out_2(tri_led_driver_27_out_2),
    .out_3(tri_led_driver_27_out_3), .out_4(tri_led_driver_27_out_4));
  LED led_81 (.in(tri_led_driver_27_out_4));
  LED led_82 (.in(tri_led_driver_28_out_2));
  tri_led_driver tri_led_driver_28 (
    .in_1(sti_simple_ternary_inverter_3_jo1____1oj), .out_2(tri_led_driver_28_out_2),
    .out_3(tri_led_driver_28_out_3), .out_4(tri_led_driver_28_out_4));
  LED led_83 (.in(tri_led_driver_28_out_3));
  LED led_84 (.in(tri_led_driver_28_out_4));
endmodule

module STI_Simple_Ternary_Inverter (
  input  [1:0] in_1,
  output [1:0] jo1____1oj
);


  assign jo1____1oj = {in_1[0], in_1[1]};

  // Notes on the sheet:
  //   Shocking?  Click the two split/joins the wires are crossed.
endmodule

module PTI_Positive_Trinary_Inverter (
  input  [1:0] in_1,
  output [1:0] jo1____1jj
);

  wire decoder_1_out0, decoder_1_out1, decoder_1_out3;

  Decoder #(.select(2)) decoder_1 (
    .out0(decoder_1_out0), .out1(decoder_1_out1), .out2(jo1____1jj[0]), .out3(decoder_1_out3), .sel(in_1));
  or or_1 (jo1____1jj[1], decoder_1_out0, decoder_1_out1, decoder_1_out3);
endmodule

module NTI_Negative_Trinary_Inverter (
  input  [1:0] in_1,
  output [1:0] jo1____11j
);

  wire decoder_1_out0, decoder_1_out2, decoder_1_out3;

  Decoder #(.select(2)) decoder_1 (
    .out0(decoder_1_out0), .out1(jo1____11j[1]), .out2(decoder_1_out2), .out3(decoder_1_out3), .sel(in_1));
  or or_1 (jo1____11j[0], decoder_1_out0, decoder_1_out2, decoder_1_out3);
endmodule

module CU_Cycle_Up (
  input  [1:0] in_1,
  output [1:0] jo1____o1j
);

  wire decoder_1_out0, decoder_1_out2, decoder_1_out3;

  Decoder #(.select(2)) decoder_1 (
    .out0(decoder_1_out0), .out1(jo1____o1j[1]), .out2(decoder_1_out2), .out3(decoder_1_out3), .sel(in_1));
  or or_1 (jo1____o1j[0], decoder_1_out0, decoder_1_out3);
endmodule

module CD_Cycle_Down (
  input  [1:0] in_1,
  output [1:0] jo1____1jo
);

  wire decoder_1_out0, decoder_1_out1, decoder_1_out3;

  Decoder #(.select(2)) decoder_1 (
    .out0(decoder_1_out0), .out1(decoder_1_out1), .out2(jo1____1jo[0]), .out3(decoder_1_out3), .sel(in_1));
  or or_1 (jo1____1jo[1], decoder_1_out0, decoder_1_out3);
endmodule

module TNAND_3_input (
  input  [1:0] in_1,
  input  [1:0] in_2,
  input  [1:0] in_3,
  output [1:0] out_4
);

  wire decoder_1_out0, decoder_1_out1, decoder_1_out2, decoder_1_out3, decoder_2_out0, decoder_2_out1,
       decoder_2_out2, decoder_2_out3, decoder_3_out0, decoder_3_out1, decoder_3_out2, decoder_3_out3;

  Decoder #(.select(2)) decoder_1 (
    .out0(decoder_1_out0), .out1(decoder_1_out1), .out2(decoder_1_out2), .out3(decoder_1_out3), .sel(in_1));
  Decoder #(.select(2)) decoder_2 (
    .out0(decoder_2_out0), .out1(decoder_2_out1), .out2(decoder_2_out2), .out3(decoder_2_out3), .sel(in_2));
  Decoder #(.select(2)) decoder_3 (
    .out0(decoder_3_out0), .out1(decoder_3_out1), .out2(decoder_3_out2), .out3(decoder_3_out3), .sel(in_3));
  and and_1 (out_4[1], decoder_1_out1, decoder_2_out1, decoder_3_out1);
  or or_1 (out_4[0], decoder_1_out2, decoder_2_out2, decoder_3_out2);

  // Notes on the sheet:
  //   Treat 11 as 00
  //   Decoders aren't required,
  //   But they make the circuit
  //   If all inputs are 1, TNAND is -1
  //   If any input is -1, TNAND is 1
  //   Otherwise, TNAND is 0
endmodule

module TNAND_fast__3_input__unsafe (
  input  [1:0] in_1,
  input  [1:0] in_2,
  input  [1:0] in_3,
  output [1:0] out_4
);

  and and_1 (out_4[1], in_3[0], in_2[0], in_1[0]);
  or or_1 (out_4[0], in_1[1], in_2[1], in_3[1]);

  // Notes on the sheet:
  //   See notes on TNAND fast, 2 input
  //   If all inputs are 1, TNAND is -1
  //   If any input is -1, TNAND is 1
  //   Otherwise, TNAND is 0
endmodule

module TNAND_fast__2_input__unsafe (
  input  [1:0] in_1,
  input  [1:0] in_2,
  output [1:0] out_3
);

  and and_1 (out_3[1], in_1[0], in_2[0]);
  or or_1 (out_3[0], in_1[1], in_2[1]);

  // Notes on the sheet:
  //   This circuit will simulate faster.  It is unsafe in the sense that
  //   It treats 11 input as *both* 1 and -1, and generates bad output
  //   To see the bug, try the inputs 00 and 11; result should be 00.  It is 01.
  //   This is probably the right way to implement all the gates, and if I did
  //   this in real hardware I probably would.  But I'm lazy, and having the
  //   the decoders around turning 11 into 00 is safer, hides bugs.
  //   If all inputs are 1, TNAND is -1
  //   If any input is -1, TNAND is 1
  //   Otherwise, TNAND is 0
endmodule

module TNOR_3_input (
  input  [1:0] in_1,
  input  [1:0] in_2,
  input  [1:0] in_3,
  output [1:0] out_4
);

  wire decoder_1_out0, decoder_1_out1, decoder_1_out2, decoder_1_out3, decoder_2_out0, decoder_2_out1,
       decoder_2_out2, decoder_2_out3, decoder_3_out0, decoder_3_out1, decoder_3_out2, decoder_3_out3;

  Decoder #(.select(2)) decoder_1 (
    .out0(decoder_1_out0), .out1(decoder_1_out1), .out2(decoder_1_out2), .out3(decoder_1_out3), .sel(in_1));
  Decoder #(.select(2)) decoder_2 (
    .out0(decoder_2_out0), .out1(decoder_2_out1), .out2(decoder_2_out2), .out3(decoder_2_out3), .sel(in_2));
  Decoder #(.select(2)) decoder_3 (
    .out0(decoder_3_out0), .out1(decoder_3_out1), .out2(decoder_3_out2), .out3(decoder_3_out3), .sel(in_3));
  or or_1 (out_4[1], decoder_1_out1, decoder_2_out1, decoder_3_out1);
  and and_1 (out_4[0], decoder_1_out2, decoder_2_out2, decoder_3_out2);

  // Notes on the sheet:
  //   Treat 11 as 00
  //   Decoders aren't required,
  //   But they make the circuit
  //   If any input is 1, TNOR is -1
  //   If all inputs are -1, TNOR is 1
  //   Otherwise, TNOR is 0
endmodule

module TNOR_fast__2_input__unsafe (
  input  [1:0] in_1,
  input  [1:0] in_2,
  output [1:0] out_3
);

  and and_1 (out_3[0], in_1[1], in_2[1]);
  or or_1 (out_3[1], in_2[0], in_1[0]);

  // Notes on the sheet:
  //   See note on TNAND fast
  //   If all inputs are -1, TNOR is 1
  //   If any input is 1, TNOR is -1
  //   Otherwise, TNOR is 0
endmodule

module TAND__min__3_input (
  input  [1:0] in_1,
  input  [1:0] in_2,
  input  [1:0] in_3,
  output [1:0] out_4
);

  wire decoder_1_out0, decoder_1_out1, decoder_1_out2, decoder_1_out3, decoder_2_out0, decoder_2_out1,
       decoder_2_out2, decoder_2_out3, decoder_3_out0, decoder_3_out1, decoder_3_out2, decoder_3_out3;

  Decoder #(.select(2)) decoder_1 (
    .out0(decoder_1_out0), .out1(decoder_1_out1), .out2(decoder_1_out2), .out3(decoder_1_out3), .sel(in_1));
  Decoder #(.select(2)) decoder_2 (
    .out0(decoder_2_out0), .out1(decoder_2_out1), .out2(decoder_2_out2), .out3(decoder_2_out3), .sel(in_2));
  Decoder #(.select(2)) decoder_3 (
    .out0(decoder_3_out0), .out1(decoder_3_out1), .out2(decoder_3_out2), .out3(decoder_3_out3), .sel(in_3));
  and and_1 (out_4[0], decoder_1_out1, decoder_2_out1, decoder_3_out1);
  or or_1 (out_4[1], decoder_1_out2, decoder_2_out2, decoder_3_out2);

  // Notes on the sheet:
  //   Treat 11 as 00
  //   Decoders aren't required,
  //   But they make the circuit
  //   If all inputs are 1, min is 1
  //   If any input is -1, min is -1
  //   Otherwise, min is 0
endmodule

module TAND_fast__2_input__unsafe (
  input  [1:0] in_1,
  input  [1:0] in_2,
  output [1:0] out_3
);

  and and_1 (out_3[0], in_1[0], in_2[0]);
  or or_1 (out_3[1], in_1[1], in_2[1]);

  // Notes on the sheet:
  //   See the notes on TNAND fast
  //   If all inputs are 1, min is 1
  //   If any input is -1, min is -1
  //   Otherwise, min is 0
endmodule

module TOR__max__3_input (
  input  [1:0] in_1,
  input  [1:0] in_2,
  input  [1:0] in_3,
  output [1:0] out_4
);

  wire decoder_1_out0, decoder_1_out1, decoder_1_out2, decoder_1_out3, decoder_2_out0, decoder_2_out1,
       decoder_2_out2, decoder_2_out3, decoder_3_out0, decoder_3_out1, decoder_3_out2, decoder_3_out3;

  Decoder #(.select(2)) decoder_1 (
    .out0(decoder_1_out0), .out1(decoder_1_out1), .out2(decoder_1_out2), .out3(decoder_1_out3), .sel(in_1));
  Decoder #(.select(2)) decoder_2 (
    .out0(decoder_2_out0), .out1(decoder_2_out1), .out2(decoder_2_out2), .out3(decoder_2_out3), .sel(in_2));
  Decoder #(.select(2)) decoder_3 (
    .out0(decoder_3_out0), .out1(decoder_3_out1), .out2(decoder_3_out2), .out3(decoder_3_out3), .sel(in_3));
  or or_1 (out_4[0], decoder_1_out1, decoder_2_out1, decoder_3_out1);
  and and_1 (out_4[1], decoder_1_out2, decoder_2_out2, decoder_3_out2);

  // Notes on the sheet:
  //   Treat 11 as 00
  //   Decoders aren't required,
  //   But they make the circuit
  //   If any input is 1, max is 1
  //   If all inputs are -1, max is -1
  //   Otherwise, max is 0
endmodule

module _3_1_MUX (
  input  [1:0] In1,
  input  [1:0] In0,
  input  [1:0] Inj,
  input  [1:0] select,
  output [1:0] \output 
);

  wire [1:0] nti_negative_trinary_inverter_1_jo1____11j, pti_positive_trinary_inverter_1_jo1____1jj,
       sti_simple_ternary_inverter_1_jo1____1oj, tnand_fast_2_input_unsafe_1_out_3,
       tnand_fast_2_input_unsafe_2_out_3, tnand_fast_2_input_unsafe_3_out_3, tnor_fast_2_input_unsafe_1_out_3;

  STI_Simple_Ternary_Inverter sti_simple_ternary_inverter_1 (
    .in_1(nti_negative_trinary_inverter_1_jo1____11j), .jo1____1oj(sti_simple_ternary_inverter_1_jo1____1oj));
  NTI_Negative_Trinary_Inverter nti_negative_trinary_inverter_1 (
    .in_1(select), .jo1____11j(nti_negative_trinary_inverter_1_jo1____11j));
  TNOR_fast__2_input__unsafe tnor_fast_2_input_unsafe_1 (
    .in_1(sti_simple_ternary_inverter_1_jo1____1oj), .in_2(pti_positive_trinary_inverter_1_jo1____1jj),
    .out_3(tnor_fast_2_input_unsafe_1_out_3));
  PTI_Positive_Trinary_Inverter pti_positive_trinary_inverter_1 (
    .in_1(select), .jo1____1jj(pti_positive_trinary_inverter_1_jo1____1jj));
  TNAND_fast__2_input__unsafe tnand_fast_2_input_unsafe_1 (
    .in_1(In1), .in_2(sti_simple_ternary_inverter_1_jo1____1oj), .out_3(tnand_fast_2_input_unsafe_1_out_3));
  TNAND_fast__2_input__unsafe tnand_fast_2_input_unsafe_2 (
    .in_1(In0), .in_2(tnor_fast_2_input_unsafe_1_out_3), .out_3(tnand_fast_2_input_unsafe_2_out_3));
  TNAND_fast__2_input__unsafe tnand_fast_2_input_unsafe_3 (
    .in_1(Inj), .in_2(pti_positive_trinary_inverter_1_jo1____1jj), .out_3(tnand_fast_2_input_unsafe_3_out_3));
  TNAND_fast__3_input__unsafe tnand_fast_3_input_unsafe_1 (
    .in_1(tnand_fast_2_input_unsafe_1_out_3), .in_2(tnand_fast_2_input_unsafe_2_out_3),
    .in_3(tnand_fast_2_input_unsafe_3_out_3), .out_4(\output ));
endmodule

module _1_3_decoder (
  input  [1:0] S,
  output [1:0] if__S__1__j_else_1,
  output [1:0] if__S__0__j_else_1,
  output [1:0] if__S__j__j_else_1
);

  wire [1:0] nti_negative_trinary_inverter_1_jo1____11j;

  STI_Simple_Ternary_Inverter sti_simple_ternary_inverter_1 (
    .in_1(nti_negative_trinary_inverter_1_jo1____11j), .jo1____1oj(if__S__1__j_else_1));
  NTI_Negative_Trinary_Inverter nti_negative_trinary_inverter_1 (
    .in_1(S), .jo1____11j(nti_negative_trinary_inverter_1_jo1____11j));
  TNOR_fast__2_input__unsafe tnor_fast_2_input_unsafe_1 (
    .in_1(if__S__1__j_else_1), .in_2(if__S__j__j_else_1), .out_3(if__S__0__j_else_1));
  PTI_Positive_Trinary_Inverter pti_positive_trinary_inverter_1 (.in_1(S), .jo1____1jj(if__S__j__j_else_1));

  // Notes on the sheet:
  //   See 3:1 MUX to see one way to use outputs
endmodule

module _6t_Register (
  input  [11:0] D,
  input  [1:0] clock,
  output [11:0] Q
);

  Register__master_slave_D_latch register_master_slave_d_latch_1 (
    .D(D[11:10]), .Clock__pulse__latch_in_on_rising_edge__out_on_falling(clock), .Q(Q[11:10]));
  Register__master_slave_D_latch register_master_slave_d_latch_2 (
    .D(D[9:8]), .Clock__pulse__latch_in_on_rising_edge__out_on_falling(clock), .Q(Q[9:8]));
  Register__master_slave_D_latch register_master_slave_d_latch_3 (
    .D(D[7:6]), .Clock__pulse__latch_in_on_rising_edge__out_on_falling(clock), .Q(Q[7:6]));
  Register__master_slave_D_latch register_master_slave_d_latch_4 (
    .D(D[5:4]), .Clock__pulse__latch_in_on_rising_edge__out_on_falling(clock), .Q(Q[5:4]));
  Register__master_slave_D_latch register_master_slave_d_latch_5 (
    .D(D[3:2]), .Clock__pulse__latch_in_on_rising_edge__out_on_falling(clock), .Q(Q[3:2]));
  Register__master_slave_D_latch register_master_slave_d_latch_6 (
    .D(D[1:0]), .Clock__pulse__latch_in_on_rising_edge__out_on_falling(clock), .Q(Q[1:0]));
endmodule

module D_Latch__level_triggered (
  input  [1:0] D,
  input  [1:0] E_1,
  output [1:0] Q
);

  wire [1:0] nti_negative_trinary_inverter_1_jo1____11j, sti_simple_ternary_inverter_1_jo1____1oj,
       tnand_3_input_1_out_4, tnand_fast_2_input_unsafe_1_out_3;

  NTI_Negative_Trinary_Inverter nti_negative_trinary_inverter_1 (
    .in_1(E_1), .jo1____11j(nti_negative_trinary_inverter_1_jo1____11j));
  STI_Simple_Ternary_Inverter sti_simple_ternary_inverter_1 (
    .in_1(nti_negative_trinary_inverter_1_jo1____11j), .jo1____1oj(sti_simple_ternary_inverter_1_jo1____1oj));
  TNAND_3_input tnand_3_input_1 (
    .in_1(D), .in_2(D), .in_3(sti_simple_ternary_inverter_1_jo1____1oj), .out_4(tnand_3_input_1_out_4));
  TNAND_fast__2_input__unsafe tnand_fast_2_input_unsafe_1 (
    .in_1(nti_negative_trinary_inverter_1_jo1____11j), .in_2(Q), .out_3(tnand_fast_2_input_unsafe_1_out_3));
  TNAND_fast__2_input__unsafe tnand_fast_2_input_unsafe_2 (
    .in_1(tnand_3_input_1_out_4), .in_2(tnand_fast_2_input_unsafe_1_out_3), .out_3(Q));
endmodule

module Register__master_slave_D_latch (
  input  [1:0] D,
  input  [1:0] Clock__pulse__latch_in_on_rising_edge__out_on_falling,
  output [1:0] Q
);

  wire [1:0] d_latch_level_triggered_1_q, nti_negative_trinary_inverter_1_jo1____11j,
       sti_simple_ternary_inverter_1_jo1____1oj;

  STI_Simple_Ternary_Inverter sti_simple_ternary_inverter_1 (
    .in_1(nti_negative_trinary_inverter_1_jo1____11j), .jo1____1oj(sti_simple_ternary_inverter_1_jo1____1oj));
  D_Latch__level_triggered d_latch_level_triggered_1 (
    .D(D), .E_1(sti_simple_ternary_inverter_1_jo1____1oj), .Q(d_latch_level_triggered_1_q));
  D_Latch__level_triggered d_latch_level_triggered_2 (
    .D(d_latch_level_triggered_1_q), .E_1(nti_negative_trinary_inverter_1_jo1____11j), .Q(Q));
  NTI_Negative_Trinary_Inverter nti_negative_trinary_inverter_1 (
    .in_1(Clock__pulse__latch_in_on_rising_edge__out_on_falling),
    .jo1____11j(nti_negative_trinary_inverter_1_jo1____11j));
endmodule

module D_Latch_w__leds (
  input  [1:0] D,
  input  [1:0] E_1,
  output [1:0] Q
);

  wire tri_led_driver_1_out_2, tri_led_driver_1_out_3, tri_led_driver_1_out_4, tri_led_driver_2_out_2,
       tri_led_driver_2_out_3, tri_led_driver_2_out_4, tri_led_driver_3_out_2, tri_led_driver_3_out_3,
       tri_led_driver_3_out_4, tri_led_driver_4_out_2, tri_led_driver_4_out_3, tri_led_driver_4_out_4,
       tri_led_driver_5_out_2, tri_led_driver_5_out_3, tri_led_driver_5_out_4, tri_led_driver_6_out_2,
       tri_led_driver_6_out_3, tri_led_driver_6_out_4, tri_led_driver_7_out_2, tri_led_driver_7_out_3,
       tri_led_driver_7_out_4, tri_led_driver_8_out_2, tri_led_driver_8_out_3, tri_led_driver_8_out_4;
  wire [1:0] nti_negative_trinary_inverter_1_jo1____11j, sti_simple_ternary_inverter_1_jo1____1oj,
       tnand_3_input_1_out_4, tnand_3_input_2_out_4;

  LED led_1 (.in(tri_led_driver_1_out_4));
  tri_led_driver tri_led_driver_1 (
    .in_1(D), .out_2(tri_led_driver_1_out_2), .out_3(tri_led_driver_1_out_3), .out_4(tri_led_driver_1_out_4));
  LED led_2 (.in(tri_led_driver_1_out_3));
  LED led_3 (.in(tri_led_driver_2_out_4));
  LED led_4 (.in(tri_led_driver_2_out_3));
  tri_led_driver tri_led_driver_2 (
    .in_1(E_1), .out_2(tri_led_driver_2_out_2), .out_3(tri_led_driver_2_out_3), .out_4(tri_led_driver_2_out_4));
  LED led_5 (.in(tri_led_driver_1_out_2));
  NTI_Negative_Trinary_Inverter nti_negative_trinary_inverter_1 (
    .in_1(E_1), .jo1____11j(nti_negative_trinary_inverter_1_jo1____11j));
  LED led_6 (.in(tri_led_driver_2_out_2));
  LED led_7 (.in(tri_led_driver_4_out_4));
  LED led_8 (.in(tri_led_driver_3_out_4));
  tri_led_driver tri_led_driver_3 (
    .in_1(sti_simple_ternary_inverter_1_jo1____1oj), .out_2(tri_led_driver_3_out_2),
    .out_3(tri_led_driver_3_out_3), .out_4(tri_led_driver_3_out_4));
  LED led_9 (.in(tri_led_driver_3_out_3));
  STI_Simple_Ternary_Inverter sti_simple_ternary_inverter_1 (
    .in_1(nti_negative_trinary_inverter_1_jo1____11j), .jo1____1oj(sti_simple_ternary_inverter_1_jo1____1oj));
  LED led_10 (.in(tri_led_driver_4_out_2));
  LED led_11 (.in(tri_led_driver_4_out_3));
  tri_led_driver tri_led_driver_4 (
    .in_1(nti_negative_trinary_inverter_1_jo1____11j), .out_2(tri_led_driver_4_out_2),
    .out_3(tri_led_driver_4_out_3), .out_4(tri_led_driver_4_out_4));
  LED led_12 (.in(tri_led_driver_7_out_4));
  TNAND_3_input tnand_3_input_1 (
    .in_1(D), .in_2(D), .in_3(sti_simple_ternary_inverter_1_jo1____1oj), .out_4(tnand_3_input_1_out_4));
  LED led_13 (.in(tri_led_driver_3_out_2));
  LED led_14 (.in(tri_led_driver_5_out_4));
  tri_led_driver tri_led_driver_5 (
    .in_1(tnand_3_input_1_out_4), .out_2(tri_led_driver_5_out_2), .out_3(tri_led_driver_5_out_3),
    .out_4(tri_led_driver_5_out_4));
  LED led_15 (.in(tri_led_driver_5_out_3));
  TNAND_3_input tnand_3_input_2 (
    .in_1(nti_negative_trinary_inverter_1_jo1____11j), .in_2(nti_negative_trinary_inverter_1_jo1____11j),
    .in_3(Q), .out_4(tnand_3_input_2_out_4));
  LED led_16 (.in(tri_led_driver_6_out_4));
  LED led_17 (.in(tri_led_driver_6_out_3));
  tri_led_driver tri_led_driver_6 (
    .in_1(tnand_3_input_2_out_4), .out_2(tri_led_driver_6_out_2), .out_3(tri_led_driver_6_out_3),
    .out_4(tri_led_driver_6_out_4));
  LED led_18 (.in(tri_led_driver_7_out_2));
  LED led_19 (.in(tri_led_driver_7_out_3));
  tri_led_driver tri_led_driver_7 (
    .in_1(Q), .out_2(tri_led_driver_7_out_2), .out_3(tri_led_driver_7_out_3), .out_4(tri_led_driver_7_out_4));
  LED led_20 (.in(tri_led_driver_5_out_2));
  LED led_21 (.in(tri_led_driver_6_out_2));
  TNAND_3_input tnand_3_input_3 (
    .in_1(tnand_3_input_1_out_4), .in_2(tnand_3_input_2_out_4), .in_3(tnand_3_input_2_out_4), .out_4(Q));
  LED led_22 (.in(tri_led_driver_8_out_2));
  LED led_23 (.in(tri_led_driver_8_out_4));
  tri_led_driver tri_led_driver_8 (
    .in_1(Q), .out_2(tri_led_driver_8_out_2), .out_3(tri_led_driver_8_out_3), .out_4(tri_led_driver_8_out_4));
  LED led_24 (.in(tri_led_driver_8_out_3));
endmodule

module _6t_x_18_stack (
  input  [1:0] j_pop__1_push__0_nop,
  input  [11:0] in,
  input  [1:0] clock,
  output [11:0] top_of_stack
);

  wire [11:0] multiplexer_1_out, multiplexer_2_out, multiplexer_3_out, multiplexer_4_out, multiplexer_5_out,
       multiplexer_6_out, multiplexer_7_out, multiplexer_8_out, multiplexer_9_out, multiplexer_10_out,
       multiplexer_11_out, multiplexer_12_out, multiplexer_13_out, multiplexer_14_out, multiplexer_15_out,
       multiplexer_16_out, multiplexer_17_out, multiplexer_18_out, n6t_register_2_q, n6t_register_3_q,
       n6t_register_4_q, n6t_register_5_q, n6t_register_6_q, n6t_register_7_q, n6t_register_8_q,
       n6t_register_9_q, n6t_register_10_q, n6t_register_11_q, n6t_register_12_q, n6t_register_13_q,
       n6t_register_14_q, n6t_register_15_q, n6t_register_16_q, n6t_register_17_q, n6t_register_18_q;

  Multiplexer #(.select(2), .width(12)) multiplexer_1 (
    .in0(top_of_stack), .in1(in), .in2(n6t_register_2_q), .in3(top_of_stack), .out(multiplexer_1_out),
    .sel(j_pop__1_push__0_nop));
  _6t_Register u_6t_register_1 (.D(multiplexer_1_out), .clock(clock), .Q(top_of_stack));
  Multiplexer #(.select(2), .width(12)) multiplexer_2 (
    .in0(n6t_register_2_q), .in1(top_of_stack), .in2(n6t_register_3_q), .in3(n6t_register_2_q),
    .out(multiplexer_2_out), .sel(j_pop__1_push__0_nop));
  _6t_Register u_6t_register_2 (.D(multiplexer_2_out), .clock(clock), .Q(n6t_register_2_q));
  Multiplexer #(.select(2), .width(12)) multiplexer_3 (
    .in0(n6t_register_3_q), .in1(n6t_register_2_q), .in2(n6t_register_4_q), .in3(n6t_register_3_q),
    .out(multiplexer_3_out), .sel(j_pop__1_push__0_nop));
  _6t_Register u_6t_register_3 (.D(multiplexer_3_out), .clock(clock), .Q(n6t_register_3_q));
  Multiplexer #(.select(2), .width(12)) multiplexer_4 (
    .in0(n6t_register_4_q), .in1(n6t_register_3_q), .in2(n6t_register_5_q), .in3(n6t_register_4_q),
    .out(multiplexer_4_out), .sel(j_pop__1_push__0_nop));
  _6t_Register u_6t_register_4 (.D(multiplexer_4_out), .clock(clock), .Q(n6t_register_4_q));
  Multiplexer #(.select(2), .width(12)) multiplexer_5 (
    .in0(n6t_register_5_q), .in1(n6t_register_4_q), .in2(n6t_register_6_q), .in3(n6t_register_5_q),
    .out(multiplexer_5_out), .sel(j_pop__1_push__0_nop));
  _6t_Register u_6t_register_5 (.D(multiplexer_5_out), .clock(clock), .Q(n6t_register_5_q));
  Multiplexer #(.select(2), .width(12)) multiplexer_6 (
    .in0(n6t_register_6_q), .in1(n6t_register_5_q), .in2(n6t_register_7_q), .in3(n6t_register_6_q),
    .out(multiplexer_6_out), .sel(j_pop__1_push__0_nop));
  _6t_Register u_6t_register_6 (.D(multiplexer_6_out), .clock(clock), .Q(n6t_register_6_q));
  Multiplexer #(.select(2), .width(12)) multiplexer_7 (
    .in0(n6t_register_7_q), .in1(n6t_register_6_q), .in2(n6t_register_8_q), .in3(n6t_register_7_q),
    .out(multiplexer_7_out), .sel(j_pop__1_push__0_nop));
  _6t_Register u_6t_register_7 (.D(multiplexer_7_out), .clock(clock), .Q(n6t_register_7_q));
  Multiplexer #(.select(2), .width(12)) multiplexer_8 (
    .in0(n6t_register_8_q), .in1(n6t_register_7_q), .in2(n6t_register_9_q), .in3(n6t_register_8_q),
    .out(multiplexer_8_out), .sel(j_pop__1_push__0_nop));
  _6t_Register u_6t_register_8 (.D(multiplexer_8_out), .clock(clock), .Q(n6t_register_8_q));
  Multiplexer #(.select(2), .width(12)) multiplexer_9 (
    .in0(n6t_register_9_q), .in1(n6t_register_8_q), .in2(n6t_register_10_q), .in3(n6t_register_9_q),
    .out(multiplexer_9_out), .sel(j_pop__1_push__0_nop));
  _6t_Register u_6t_register_9 (.D(multiplexer_9_out), .clock(clock), .Q(n6t_register_9_q));
  Multiplexer #(.select(2), .width(12)) multiplexer_10 (
    .in0(n6t_register_10_q), .in1(n6t_register_9_q), .in2(n6t_register_11_q), .in3(n6t_register_10_q),
    .out(multiplexer_10_out), .sel(j_pop__1_push__0_nop));
  _6t_Register u_6t_register_10 (.D(multiplexer_10_out), .clock(clock), .Q(n6t_register_10_q));
  Multiplexer #(.select(2), .width(12)) multiplexer_11 (
    .in0(n6t_register_11_q), .in1(n6t_register_10_q), .in2(n6t_register_12_q), .in3(n6t_register_11_q),
    .out(multiplexer_11_out), .sel(j_pop__1_push__0_nop));
  _6t_Register u_6t_register_11 (.D(multiplexer_11_out), .clock(clock), .Q(n6t_register_11_q));
  Multiplexer #(.select(2), .width(12)) multiplexer_12 (
    .in0(n6t_register_12_q), .in1(n6t_register_11_q), .in2(n6t_register_13_q), .in3(n6t_register_12_q),
    .out(multiplexer_12_out), .sel(j_pop__1_push__0_nop));
  _6t_Register u_6t_register_12 (.D(multiplexer_12_out), .clock(clock), .Q(n6t_register_12_q));
  Multiplexer #(.select(2), .width(12)) multiplexer_13 (
    .in0(n6t_register_13_q), .in1(n6t_register_12_q), .in2(n6t_register_14_q), .in3(n6t_register_13_q),
    .out(multiplexer_13_out), .sel(j_pop__1_push__0_nop));
  _6t_Register u_6t_register_13 (.D(multiplexer_13_out), .clock(clock), .Q(n6t_register_13_q));
  Multiplexer #(.select(2), .width(12)) multiplexer_14 (
    .in0(n6t_register_14_q), .in1(n6t_register_13_q), .in2(n6t_register_15_q), .in3(n6t_register_14_q),
    .out(multiplexer_14_out), .sel(j_pop__1_push__0_nop));
  _6t_Register u_6t_register_14 (.D(multiplexer_14_out), .clock(clock), .Q(n6t_register_14_q));
  Multiplexer #(.select(2), .width(12)) multiplexer_15 (
    .in0(n6t_register_15_q), .in1(n6t_register_14_q), .in2(n6t_register_16_q), .in3(n6t_register_15_q),
    .out(multiplexer_15_out), .sel(j_pop__1_push__0_nop));
  _6t_Register u_6t_register_15 (.D(multiplexer_15_out), .clock(clock), .Q(n6t_register_15_q));
  Multiplexer #(.select(2), .width(12)) multiplexer_16 (
    .in0(n6t_register_16_q), .in1(n6t_register_15_q), .in2(n6t_register_17_q), .in3(n6t_register_16_q),
    .out(multiplexer_16_out), .sel(j_pop__1_push__0_nop));
  _6t_Register u_6t_register_16 (.D(multiplexer_16_out), .clock(clock), .Q(n6t_register_16_q));
  Multiplexer #(.select(2), .width(12)) multiplexer_17 (
    .in0(n6t_register_17_q), .in1(n6t_register_16_q), .in2(n6t_register_18_q), .in3(n6t_register_17_q),
    .out(multiplexer_17_out), .sel(j_pop__1_push__0_nop));
  _6t_Register u_6t_register_17 (.D(multiplexer_17_out), .clock(clock), .Q(n6t_register_17_q));
  Multiplexer #(.select(2), .width(12)) multiplexer_18 (
    .in0(n6t_register_18_q), .in1(n6t_register_17_q), .in2(top_of_stack), .in3(n6t_register_18_q),
    .out(multiplexer_18_out), .sel(j_pop__1_push__0_nop));
  _6t_Register u_6t_register_18 (.D(multiplexer_18_out), .clock(clock), .Q(n6t_register_18_q));

  // Notes on the sheet:
  //   Lazy and cheating to use MUXes here I think.
  //   It is often called a stack, and we usually think about it as a stack, but it's actually a ring.  18 pops in a row is a long slow nop.
endmodule

module _2t_to_7seg_driver (
  input  [3:0] in_1,
  output out_2,
  output out_3,
  output out_4,
  output out_5,
  output out_6,
  output out_7,
  output out_8,
  output out_9
);

  ROM #(.addrWidth(4)) rom_1 (
    .addr(in_1), .data({out_9, out_8, out_7, out_6, out_5, out_4, out_3, out_2}));  // open: sel

  // Notes on the sheet:
  //   contents of rom_1 (hex, n*v repeats v):
  //   fc 60 ee fc f2 66 da f2 9c 3e 7a 9c fc 60 ee fc
endmodule

module _6t_counter (
  input  [1:0] in_1,
  input  [1:0] in_2,
  output [11:0] out_3
);

  wire [1:0] cu_cycle_up_1_jo1____o1j, cu_cycle_up_2_jo1____o1j, cu_cycle_up_3_jo1____o1j,
       cu_cycle_up_4_jo1____o1j, cu_cycle_up_5_jo1____o1j, cu_cycle_up_6_jo1____o1j,
       nti_negative_trinary_inverter_1_jo1____11j, nti_negative_trinary_inverter_2_jo1____11j,
       nti_negative_trinary_inverter_3_jo1____11j, nti_negative_trinary_inverter_4_jo1____11j,
       nti_negative_trinary_inverter_5_jo1____11j, nti_negative_trinary_inverter_6_jo1____11j,
       sti_simple_ternary_inverter_1_jo1____1oj, sti_simple_ternary_inverter_2_jo1____1oj,
       sti_simple_ternary_inverter_3_jo1____1oj, sti_simple_ternary_inverter_4_jo1____1oj,
       sti_simple_ternary_inverter_5_jo1____1oj, sti_simple_ternary_inverter_6_jo1____1oj,
       tand_fast_2_input_unsafe_1_out_3, tand_fast_2_input_unsafe_2_out_3, tand_fast_2_input_unsafe_3_out_3,
       tand_fast_2_input_unsafe_4_out_3, tnand_3_input_1_out_4, tnand_3_input_2_out_4, tnand_3_input_3_out_4,
       tnand_3_input_4_out_4, tnand_3_input_5_out_4, tnand_3_input_6_out_4,
       tnand_fast_2_input_unsafe_1_out_3, tnand_fast_2_input_unsafe_2_out_3,
       tnand_fast_2_input_unsafe_3_out_3, tnand_fast_2_input_unsafe_4_out_3,
       tnand_fast_2_input_unsafe_5_out_3, tnand_fast_2_input_unsafe_6_out_3,
       tnand_fast_2_input_unsafe_7_out_3, tnand_fast_2_input_unsafe_8_out_3,
       tnand_fast_2_input_unsafe_9_out_3, tnand_fast_2_input_unsafe_10_out_3;

  NTI_Negative_Trinary_Inverter nti_negative_trinary_inverter_1 (
    .in_1(in_2), .jo1____11j(nti_negative_trinary_inverter_1_jo1____11j));
  TNAND_3_input tnand_3_input_1 (
    .in_1(tnand_fast_2_input_unsafe_1_out_3), .in_2(nti_negative_trinary_inverter_1_jo1____11j),
    .in_3(tnand_fast_2_input_unsafe_2_out_3), .out_4(tnand_3_input_1_out_4));
  // Probe on nti_negative_trinary_inverter_1_jo1____11j
  TNAND_fast__2_input__unsafe tnand_fast_2_input_unsafe_1 (
    .in_1(sti_simple_ternary_inverter_1_jo1____1oj), .in_2(cu_cycle_up_1_jo1____o1j),
    .out_3(tnand_fast_2_input_unsafe_1_out_3));
  CU_Cycle_Up cu_cycle_up_1 (.in_1(out_3[11:10]), .jo1____o1j(cu_cycle_up_1_jo1____o1j));
  STI_Simple_Ternary_Inverter sti_simple_ternary_inverter_1 (
    .in_1(nti_negative_trinary_inverter_2_jo1____11j), .jo1____1oj(sti_simple_ternary_inverter_1_jo1____1oj));
  NTI_Negative_Trinary_Inverter nti_negative_trinary_inverter_2 (
    .in_1(tand_fast_2_input_unsafe_1_out_3), .jo1____11j(nti_negative_trinary_inverter_2_jo1____11j));
  Register__master_slave_D_latch register_master_slave_d_latch_1 (
    .D(tnand_3_input_1_out_4), .Clock__pulse__latch_in_on_rising_edge__out_on_falling(in_1), .Q(out_3[11:10]));
  TNAND_fast__2_input__unsafe tnand_fast_2_input_unsafe_2 (
    .in_1(out_3[11:10]), .in_2(nti_negative_trinary_inverter_2_jo1____11j),
    .out_3(tnand_fast_2_input_unsafe_2_out_3));
  TAND_fast__2_input__unsafe tand_fast_2_input_unsafe_1 (
    .in_1(tand_fast_2_input_unsafe_2_out_3), .in_2(out_3[9:8]), .out_3(tand_fast_2_input_unsafe_1_out_3));
  TNAND_3_input tnand_3_input_2 (
    .in_1(tnand_fast_2_input_unsafe_3_out_3), .in_2(nti_negative_trinary_inverter_1_jo1____11j),
    .in_3(tnand_fast_2_input_unsafe_4_out_3), .out_4(tnand_3_input_2_out_4));
  TNAND_fast__2_input__unsafe tnand_fast_2_input_unsafe_3 (
    .in_1(sti_simple_ternary_inverter_2_jo1____1oj), .in_2(cu_cycle_up_2_jo1____o1j),
    .out_3(tnand_fast_2_input_unsafe_3_out_3));
  TNAND_fast__2_input__unsafe tnand_fast_2_input_unsafe_4 (
    .in_1(out_3[9:8]), .in_2(nti_negative_trinary_inverter_3_jo1____11j),
    .out_3(tnand_fast_2_input_unsafe_4_out_3));
  CU_Cycle_Up cu_cycle_up_2 (.in_1(out_3[9:8]), .jo1____o1j(cu_cycle_up_2_jo1____o1j));
  STI_Simple_Ternary_Inverter sti_simple_ternary_inverter_2 (
    .in_1(nti_negative_trinary_inverter_3_jo1____11j), .jo1____1oj(sti_simple_ternary_inverter_2_jo1____1oj));
  NTI_Negative_Trinary_Inverter nti_negative_trinary_inverter_3 (
    .in_1(tand_fast_2_input_unsafe_2_out_3), .jo1____11j(nti_negative_trinary_inverter_3_jo1____11j));
  Register__master_slave_D_latch register_master_slave_d_latch_2 (
    .D(tnand_3_input_2_out_4), .Clock__pulse__latch_in_on_rising_edge__out_on_falling(in_1), .Q(out_3[9:8]));
  TNAND_fast__2_input__unsafe tnand_fast_2_input_unsafe_5 (
    .in_1(sti_simple_ternary_inverter_3_jo1____1oj), .in_2(cu_cycle_up_3_jo1____o1j),
    .out_3(tnand_fast_2_input_unsafe_5_out_3));
  STI_Simple_Ternary_Inverter sti_simple_ternary_inverter_3 (
    .in_1(nti_negative_trinary_inverter_4_jo1____11j), .jo1____1oj(sti_simple_ternary_inverter_3_jo1____1oj));
  TAND_fast__2_input__unsafe tand_fast_2_input_unsafe_2 (
    .in_1(tand_fast_2_input_unsafe_3_out_3), .in_2(out_3[7:6]), .out_3(tand_fast_2_input_unsafe_2_out_3));
  TNAND_3_input tnand_3_input_3 (
    .in_1(tnand_fast_2_input_unsafe_5_out_3), .in_2(nti_negative_trinary_inverter_1_jo1____11j),
    .in_3(tnand_fast_2_input_unsafe_6_out_3), .out_4(tnand_3_input_3_out_4));
  TNAND_fast__2_input__unsafe tnand_fast_2_input_unsafe_6 (
    .in_1(out_3[7:6]), .in_2(nti_negative_trinary_inverter_4_jo1____11j),
    .out_3(tnand_fast_2_input_unsafe_6_out_3));
  CU_Cycle_Up cu_cycle_up_3 (.in_1(out_3[7:6]), .jo1____o1j(cu_cycle_up_3_jo1____o1j));
  NTI_Negative_Trinary_Inverter nti_negative_trinary_inverter_4 (
    .in_1(tand_fast_2_input_unsafe_3_out_3), .jo1____11j(nti_negative_trinary_inverter_4_jo1____11j));
  TAND_fast__2_input__unsafe tand_fast_2_input_unsafe_3 (
    .in_1(tand_fast_2_input_unsafe_4_out_3), .in_2(out_3[5:4]), .out_3(tand_fast_2_input_unsafe_3_out_3));
  Register__master_slave_D_latch register_master_slave_d_latch_3 (
    .D(tnand_3_input_3_out_4), .Clock__pulse__latch_in_on_rising_edge__out_on_falling(in_1), .Q(out_3[7:6]));
  TNAND_fast__2_input__unsafe tnand_fast_2_input_unsafe_7 (
    .in_1(sti_simple_ternary_inverter_4_jo1____1oj), .in_2(cu_cycle_up_4_jo1____o1j),
    .out_3(tnand_fast_2_input_unsafe_7_out_3));
  STI_Simple_Ternary_Inverter sti_simple_ternary_inverter_4 (
    .in_1(nti_negative_trinary_inverter_5_jo1____11j), .jo1____1oj(sti_simple_ternary_inverter_4_jo1____1oj));
  NTI_Negative_Trinary_Inverter nti_negative_trinary_inverter_5 (
    .in_1(tand_fast_2_input_unsafe_4_out_3), .jo1____11j(nti_negative_trinary_inverter_5_jo1____11j));
  Register__master_slave_D_latch register_master_slave_d_latch_4 (
    .D(tnand_3_input_4_out_4), .Clock__pulse__latch_in_on_rising_edge__out_on_falling(in_1), .Q(out_3[5:4]));
  TNAND_3_input tnand_3_input_4 (
    .in_1(tnand_fast_2_input_unsafe_7_out_3), .in_2(nti_negative_trinary_inverter_1_jo1____11j),
    .in_3(tnand_fast_2_input_unsafe_8_out_3), .out_4(tnand_3_input_4_out_4));
  TNAND_fast__2_input__unsafe tnand_fast_2_input_unsafe_8 (
    .in_1(out_3[5:4]), .in_2(nti_negative_trinary_inverter_5_jo1____11j),
    .out_3(tnand_fast_2_input_unsafe_8_out_3));
  CU_Cycle_Up cu_cycle_up_4 (.in_1(out_3[5:4]), .jo1____o1j(cu_cycle_up_4_jo1____o1j));
  TAND_fast__2_input__unsafe tand_fast_2_input_unsafe_4 (
    .in_1(out_3[1:0]), .in_2(out_3[3:2]), .out_3(tand_fast_2_input_unsafe_4_out_3));
  TNAND_3_input tnand_3_input_5 (
    .in_1(tnand_fast_2_input_unsafe_9_out_3), .in_2(nti_negative_trinary_inverter_1_jo1____11j),
    .in_3(tnand_fast_2_input_unsafe_10_out_3), .out_4(tnand_3_input_5_out_4));
  TNAND_fast__2_input__unsafe tnand_fast_2_input_unsafe_9 (
    .in_1(sti_simple_ternary_inverter_5_jo1____1oj), .in_2(cu_cycle_up_5_jo1____o1j),
    .out_3(tnand_fast_2_input_unsafe_9_out_3));
  CU_Cycle_Up cu_cycle_up_5 (.in_1(out_3[3:2]), .jo1____o1j(cu_cycle_up_5_jo1____o1j));
  STI_Simple_Ternary_Inverter sti_simple_ternary_inverter_5 (
    .in_1(nti_negative_trinary_inverter_6_jo1____11j), .jo1____1oj(sti_simple_ternary_inverter_5_jo1____1oj));
  NTI_Negative_Trinary_Inverter nti_negative_trinary_inverter_6 (
    .in_1(out_3[1:0]), .jo1____11j(nti_negative_trinary_inverter_6_jo1____11j));
  Register__master_slave_D_latch register_master_slave_d_latch_5 (
    .D(tnand_3_input_5_out_4), .Clock__pulse__latch_in_on_rising_edge__out_on_falling(in_1), .Q(out_3[3:2]));
  TNAND_fast__2_input__unsafe tnand_fast_2_input_unsafe_10 (
    .in_1(out_3[3:2]), .in_2(nti_negative_trinary_inverter_6_jo1____11j),
    .out_3(tnand_fast_2_input_unsafe_10_out_3));
  TNAND_3_input tnand_3_input_6 (
    .in_1(sti_simple_ternary_inverter_6_jo1____1oj), .in_2(nti_negative_trinary_inverter_1_jo1____11j),
    .in_3(sti_simple_ternary_inverter_6_jo1____1oj), .out_4(tnand_3_input_6_out_4));
  STI_Simple_Ternary_Inverter sti_simple_ternary_inverter_6 (
    .in_1(cu_cycle_up_6_jo1____o1j), .jo1____1oj(sti_simple_ternary_inverter_6_jo1____1oj));
  CU_Cycle_Up cu_cycle_up_6 (.in_1(out_3[1:0]), .jo1____o1j(cu_cycle_up_6_jo1____o1j));
  Register__master_slave_D_latch register_master_slave_d_latch_6 (
    .D(tnand_3_input_6_out_4), .Clock__pulse__latch_in_on_rising_edge__out_on_falling(in_1), .Q(out_3[1:0]));
endmodule

module keyboard_input (
  input  in_1,
  input  in_2,
  input  in_3,
  input  in_4,
  input  in_5,
  input  in_6,
  input  in_7,
  input  in_8,
  input  in_9,
  output [11:0] out_10
);

  wire or_2_out;
  wire [0:0] or_7_out;
  wire [1:0] nti_negative_trinary_inverter_1_jo1____11j, or_1_out, or_4_out;

  // Probe on out_10[11:10]
  Register__master_slave_D_latch register_master_slave_d_latch_1 (
    .D(out_10[7:6]),
    .Clock__pulse__latch_in_on_rising_edge__out_on_falling(nti_negative_trinary_inverter_1_jo1____11j),
    .Q(out_10[11:10]));
  // Probe on out_10[9:8]
  Register__master_slave_D_latch register_master_slave_d_latch_2 (
    .D(out_10[5:4]),
    .Clock__pulse__latch_in_on_rising_edge__out_on_falling(nti_negative_trinary_inverter_1_jo1____11j),
    .Q(out_10[9:8]));
  // Probe on out_10[7:6]
  Register__master_slave_D_latch register_master_slave_d_latch_3 (
    .D(out_10[3:2]),
    .Clock__pulse__latch_in_on_rising_edge__out_on_falling(nti_negative_trinary_inverter_1_jo1____11j),
    .Q(out_10[7:6]));
  // Probe on out_10[5:4]
  Register__master_slave_D_latch register_master_slave_d_latch_4 (
    .D(out_10[1:0]),
    .Clock__pulse__latch_in_on_rising_edge__out_on_falling(nti_negative_trinary_inverter_1_jo1____11j),
    .Q(out_10[5:4]));
  // Probe on out_10[3:2]
  Register__master_slave_D_latch register_master_slave_d_latch_5 (
    .D(or_1_out),
    .Clock__pulse__latch_in_on_rising_edge__out_on_falling(nti_negative_trinary_inverter_1_jo1____11j),
    .Q(out_10[3:2]));
  Register__master_slave_D_latch register_master_slave_d_latch_6 (
    .D(or_4_out),
    .Clock__pulse__latch_in_on_rising_edge__out_on_falling(nti_negative_trinary_inverter_1_jo1____11j),
    .Q(out_10[1:0]));
  // Probe on out_10[1:0]
  NTI_Negative_Trinary_Inverter nti_negative_trinary_inverter_1 (
    .in_1({1'b0, or_7_out[0]}), .jo1____11j(nti_negative_trinary_inverter_1_jo1____11j));
  or or_1 (or_1_out[0], in_1, in_2, in_3);
  or or_2 (or_2_out, in_4, in_5, in_6);
  or or_3 (or_1_out[1], in_7, in_8, in_9);
  or or_4 (or_4_out[0], in_3, in_6, in_9);
  // OR_Gate or_5 has open pins: in1=in_2, in2=in_5, in3=in_8, out=open
  or or_6 (or_4_out[1], in_1, in_4, in_7);
  or or_7 (or_7_out[0], or_1_out[0], or_2_out, or_1_out[1]);
endmodule

module tri_led_driver (
  input  [1:0] in_1,
  output out_2,
  output out_3,
  output out_4
);

  wire decoder_1_out0, decoder_1_out3;

  Decoder #(.select(2)) decoder_1 (
    .out0(decoder_1_out0), .out1(out_2), .out2(out_4), .out3(decoder_1_out3), .sel(in_1));
  or or_1 (out_3, decoder_1_out0, decoder_1_out3);
endmodule

module rs_latch_notes (
  input  [1:0] in_1,
  input  [1:0] in_2,
  input  [1:0] in_3,
  input  [1:0] in_4,
  input  [1:0] in_5,
  input  [1:0] in_6,
  input  [1:0] in_7,
  input  [1:0] in_8,
  input  [1:0] in_9
);

  wire tri_led_driver_1_out_2, tri_led_driver_1_out_3, tri_led_driver_1_out_4, tri_led_driver_2_out_2,
       tri_led_driver_2_out_3, tri_led_driver_2_out_4, tri_led_driver_3_out_2, tri_led_driver_3_out_3,
       tri_led_driver_3_out_4, tri_led_driver_4_out_2, tri_led_driver_4_out_3, tri_led_driver_4_out_4,
       tri_led_driver_5_out_2, tri_led_driver_5_out_3, tri_led_driver_5_out_4, tri_led_driver_6_out_2,
       tri_led_driver_6_out_3, tri_led_driver_6_out_4, tri_led_driver_7_out_2, tri_led_driver_7_out_3,
       tri_led_driver_7_out_4, tri_led_driver_8_out_2, tri_led_driver_8_out_3, tri_led_driver_8_out_4,
       tri_led_driver_9_out_2, tri_led_driver_9_out_3, tri_led_driver_9_out_4, tri_led_driver_10_out_2,
       tri_led_driver_10_out_3, tri_led_driver_10_out_4, tri_led_driver_11_out_2, tri_led_driver_11_out_3,
       tri_led_driver_11_out_4, tri_led_driver_12_out_2, tri_led_driver_12_out_3, tri_led_driver_12_out_4,
       tri_led_driver_13_out_2, tri_led_driver_13_out_3, tri_led_driver_13_out_4, tri_led_driver_14_out_2,
       tri_led_driver_14_out_3, tri_led_driver_14_out_4, tri_led_driver_15_out_2, tri_led_driver_15_out_3,
       tri_led_driver_15_out_4, tri_led_driver_16_out_2, tri_led_driver_16_out_3, tri_led_driver_16_out_4,
       tri_led_driver_17_out_2, tri_led_driver_17_out_3, tri_led_driver_17_out_4, tri_led_driver_18_out_2,
       tri_led_driver_18_out_3, tri_led_driver_18_out_4;
  wire [1:0] pti_positive_trinary_inverter_1_jo1____1jj, pti_positive_trinary_inverter_2_jo1____1jj,
       tand_min_3_input_1_out_4, tand_min_3_input_2_out_4, tnand_3_input_1_out_4, tnand_3_input_2_out_4,
       tnand_3_input_3_out_4, tnand_3_input_4_out_4, tnand_3_input_5_out_4, tnor_3_input_1_out_4,
       tnor_3_input_2_out_4;

  LED led_1 (.in(tri_led_driver_1_out_2));
  tri_led_driver tri_led_driver_1 (
    .in_1(in_2), .out_2(tri_led_driver_1_out_2), .out_3(tri_led_driver_1_out_3),
    .out_4(tri_led_driver_1_out_4));
  LED led_2 (.in(tri_led_driver_1_out_3));
  LED led_3 (.in(tri_led_driver_1_out_4));
  LED led_4 (.in(tri_led_driver_2_out_2));
  LED led_5 (.in(tri_led_driver_2_out_3));
  tri_led_driver tri_led_driver_2 (
    .in_1(in_3), .out_2(tri_led_driver_2_out_2), .out_3(tri_led_driver_2_out_3),
    .out_4(tri_led_driver_2_out_4));
  LED led_6 (.in(tri_led_driver_2_out_4));
  LED led_7 (.in(tri_led_driver_3_out_2));
  LED led_8 (.in(tri_led_driver_3_out_3));
  tri_led_driver tri_led_driver_3 (
    .in_1(in_6), .out_2(tri_led_driver_3_out_2), .out_3(tri_led_driver_3_out_3),
    .out_4(tri_led_driver_3_out_4));
  LED led_9 (.in(tri_led_driver_3_out_4));
  LED led_10 (.in(tri_led_driver_4_out_2));
  LED led_11 (.in(tri_led_driver_4_out_3));
  tri_led_driver tri_led_driver_4 (
    .in_1(in_7), .out_2(tri_led_driver_4_out_2), .out_3(tri_led_driver_4_out_3),
    .out_4(tri_led_driver_4_out_4));
  LED led_12 (.in(tri_led_driver_4_out_4));
  LED led_13 (.in(tri_led_driver_5_out_2));
  LED led_14 (.in(tri_led_driver_5_out_3));
  tri_led_driver tri_led_driver_5 (
    .in_1(in_8), .out_2(tri_led_driver_5_out_2), .out_3(tri_led_driver_5_out_3),
    .out_4(tri_led_driver_5_out_4));
  LED led_15 (.in(tri_led_driver_5_out_4));
  LED led_16 (.in(tri_led_driver_6_out_2));
  LED led_17 (.in(tri_led_driver_6_out_3));
  tri_led_driver tri_led_driver_6 (
    .in_1(in_9), .out_2(tri_led_driver_6_out_2), .out_3(tri_led_driver_6_out_3),
    .out_4(tri_led_driver_6_out_4));
  LED led_18 (.in(tri_led_driver_6_out_4));
  TNAND_3_input tnand_3_input_1 (.in_1(tnand_3_input_2_out_4), .in_2(in_2), .in_3(in_2), .out_4(tnand_3_input_1_out_4));
  TNAND_3_input tnand_3_input_2 (.in_1(in_3), .in_2(in_3), .in_3(tnand_3_input_1_out_4), .out_4(tnand_3_input_2_out_4));
  TAND__min__3_input tand_min_3_input_1 (
    .in_1(pti_positive_trinary_inverter_2_jo1____1jj), .in_2(in_6), .in_3(in_6),
    .out_4(tand_min_3_input_1_out_4));
  TAND__min__3_input tand_min_3_input_2 (
    .in_1(in_7), .in_2(in_7), .in_3(pti_positive_trinary_inverter_1_jo1____1jj),
    .out_4(tand_min_3_input_2_out_4));
  TNOR_3_input tnor_3_input_1 (.in_1(tnor_3_input_2_out_4), .in_2(in_8), .in_3(in_8), .out_4(tnor_3_input_1_out_4));
  TNOR_3_input tnor_3_input_2 (.in_1(in_9), .in_2(in_9), .in_3(tnor_3_input_1_out_4), .out_4(tnor_3_input_2_out_4));
  PTI_Positive_Trinary_Inverter pti_positive_trinary_inverter_1 (
    .in_1(tand_min_3_input_1_out_4), .jo1____1jj(pti_positive_trinary_inverter_1_jo1____1jj));
  PTI_Positive_Trinary_Inverter pti_positive_trinary_inverter_2 (
    .in_1(tand_min_3_input_2_out_4), .jo1____1jj(pti_positive_trinary_inverter_2_jo1____1jj));
  LED led_19 (.in(tri_led_driver_7_out_2));
  tri_led_driver tri_led_driver_7 (
    .in_1(tnand_3_input_1_out_4), .out_2(tri_led_driver_7_out_2), .out_3(tri_led_driver_7_out_3),
    .out_4(tri_led_driver_7_out_4));
  LED led_20 (.in(tri_led_driver_7_out_3));
  LED led_21 (.in(tri_led_driver_7_out_4));
  LED led_22 (.in(tri_led_driver_8_out_2));
  LED led_23 (.in(tri_led_driver_8_out_3));
  tri_led_driver tri_led_driver_8 (
    .in_1(tnand_3_input_2_out_4), .out_2(tri_led_driver_8_out_2), .out_3(tri_led_driver_8_out_3),
    .out_4(tri_led_driver_8_out_4));
  LED led_24 (.in(tri_led_driver_8_out_4));
  LED led_25 (.in(tri_led_driver_9_out_2));
  LED led_26 (.in(tri_led_driver_9_out_3));
  tri_led_driver tri_led_driver_9 (
    .in_1(pti_positive_trinary_inverter_1_jo1____1jj), .out_2(tri_led_driver_9_out_2),
    .out_3(tri_led_driver_9_out_3), .out_4(tri_led_driver_9_out_4));
  LED led_27 (.in(tri_led_driver_9_out_4));
  LED led_28 (.in(tri_led_driver_10_out_2));
  tri_led_driver tri_led_driver_10 (
    .in_1(pti_positive_trinary_inverter_2_jo1____1jj), .out_2(tri_led_driver_10_out_2),
    .out_3(tri_led_driver_10_out_3), .out_4(tri_led_driver_10_out_4));
  LED led_29 (.in(tri_led_driver_10_out_3));
  LED led_30 (.in(tri_led_driver_10_out_4));
  LED led_31 (.in(tri_led_driver_11_out_2));
  LED led_32 (.in(tri_led_driver_11_out_3));
  tri_led_driver tri_led_driver_11 (
    .in_1(tnor_3_input_1_out_4), .out_2(tri_led_driver_11_out_2), .out_3(tri_led_driver_11_out_3),
    .out_4(tri_led_driver_11_out_4));
  LED led_33 (.in(tri_led_driver_11_out_4));
  LED led_34 (.in(tri_led_driver_12_out_2));
  LED led_35 (.in(tri_led_driver_12_out_3));
  tri_led_driver tri_led_driver_12 (
    .in_1(tnor_3_input_2_out_4), .out_2(tri_led_driver_12_out_2), .out_3(tri_led_driver_12_out_3),
    .out_4(tri_led_driver_12_out_4));
  LED led_36 (.in(tri_led_driver_12_out_4));
  LED led_37 (.in(tri_led_driver_13_out_2));
  LED led_38 (.in(tri_led_driver_13_out_4));
  LED led_39 (.in(tri_led_driver_14_out_2));
  LED led_40 (.in(tri_led_driver_14_out_4));
  LED led_41 (.in(tri_led_driver_15_out_2));
  LED led_42 (.in(tri_led_driver_15_out_4));
  LED led_43 (.in(tri_led_driver_13_out_3));
  tri_led_driver tri_led_driver_13 (
    .in_1(in_1), .out_2(tri_led_driver_13_out_2), .out_3(tri_led_driver_13_out_3),
    .out_4(tri_led_driver_13_out_4));
  tri_led_driver tri_led_driver_14 (
    .in_1(in_4), .out_2(tri_led_driver_14_out_2), .out_3(tri_led_driver_14_out_3),
    .out_4(tri_led_driver_14_out_4));
  LED led_44 (.in(tri_led_driver_14_out_3));
  LED led_45 (.in(tri_led_driver_15_out_3));
  tri_led_driver tri_led_driver_15 (
    .in_1(in_5), .out_2(tri_led_driver_15_out_2), .out_3(tri_led_driver_15_out_3),
    .out_4(tri_led_driver_15_out_4));
  TNAND_3_input tnand_3_input_3 (.in_1(in_1), .in_2(in_1), .in_3(tnand_3_input_4_out_4), .out_4(tnand_3_input_3_out_4));
  TNAND_3_input tnand_3_input_4 (.in_1(in_4), .in_2(in_4), .in_3(tnand_3_input_5_out_4), .out_4(tnand_3_input_4_out_4));
  TNAND_3_input tnand_3_input_5 (.in_1(in_5), .in_2(in_5), .in_3(tnand_3_input_3_out_4), .out_4(tnand_3_input_5_out_4));
  LED led_46 (.in(tri_led_driver_16_out_2));
  LED led_47 (.in(tri_led_driver_16_out_3));
  tri_led_driver tri_led_driver_16 (
    .in_1(tnand_3_input_3_out_4), .out_2(tri_led_driver_16_out_2), .out_3(tri_led_driver_16_out_3),
    .out_4(tri_led_driver_16_out_4));
  LED led_48 (.in(tri_led_driver_16_out_4));
  LED led_49 (.in(tri_led_driver_17_out_2));
  LED led_50 (.in(tri_led_driver_17_out_3));
  tri_led_driver tri_led_driver_17 (
    .in_1(tnand_3_input_4_out_4), .out_2(tri_led_driver_17_out_2), .out_3(tri_led_driver_17_out_3),
    .out_4(tri_led_driver_17_out_4));
  LED led_51 (.in(tri_led_driver_17_out_4));
  LED led_52 (.in(tri_led_driver_18_out_2));
  tri_led_driver tri_led_driver_18 (
    .in_1(tnand_3_input_5_out_4), .out_2(tri_led_driver_18_out_2), .out_3(tri_led_driver_18_out_3),
    .out_4(tri_led_driver_18_out_4));
  LED led_53 (.in(tri_led_driver_18_out_3));
  LED led_54 (.in(tri_led_driver_18_out_4));

  // Notes on the sheet:
  //   This doesn't work.  Idle in 1, doesn't show latch behavior unless move one input to -1
  //   But in that case 'glitches' to 0 before latching to -1
  //   But, is incomplete because it only has 2 stable states
  //   This does.  Idle in 0 or 1, latches when an input transitions to -1.
  //   Both -1 acts as a nor-rs latch, just shows 1 on both outputs
endmodule

module Muller_C_gate_notes (
  input  [1:0] in_1,
  input  [1:0] in_2,
  output [1:0] out_3
);

  wire tri_led_driver_1_out_2, tri_led_driver_1_out_3, tri_led_driver_1_out_4, tri_led_driver_2_out_2,
       tri_led_driver_2_out_3, tri_led_driver_2_out_4, tri_led_driver_3_out_2, tri_led_driver_3_out_3,
       tri_led_driver_3_out_4, tri_led_driver_4_out_2, tri_led_driver_4_out_3, tri_led_driver_4_out_4,
       tri_led_driver_5_out_2, tri_led_driver_5_out_3, tri_led_driver_5_out_4, tri_led_driver_6_out_2,
       tri_led_driver_6_out_3, tri_led_driver_6_out_4;
  wire [1:0] tnand_3_input_1_out_4, tnand_3_input_2_out_4, tnand_3_input_3_out_4;

  LED led_1 (.in(tri_led_driver_1_out_4));
  LED led_2 (.in(tri_led_driver_2_out_4));
  LED led_3 (.in(tri_led_driver_1_out_2));
  LED led_4 (.in(tri_led_driver_1_out_3));
  tri_led_driver tri_led_driver_1 (
    .in_1(in_1), .out_2(tri_led_driver_1_out_2), .out_3(tri_led_driver_1_out_3),
    .out_4(tri_led_driver_1_out_4));
  LED led_5 (.in(tri_led_driver_2_out_2));
  tri_led_driver tri_led_driver_2 (
    .in_1(in_2), .out_2(tri_led_driver_2_out_2), .out_3(tri_led_driver_2_out_3),
    .out_4(tri_led_driver_2_out_4));
  LED led_6 (.in(tri_led_driver_2_out_3));
  TNAND_3_input tnand_3_input_1 (.in_1(out_3), .in_2(out_3), .in_3(in_1), .out_4(tnand_3_input_1_out_4));
  LED led_7 (.in(tri_led_driver_3_out_2));
  LED led_8 (.in(tri_led_driver_3_out_4));
  tri_led_driver tri_led_driver_3 (
    .in_1(tnand_3_input_1_out_4), .out_2(tri_led_driver_3_out_2), .out_3(tri_led_driver_3_out_3),
    .out_4(tri_led_driver_3_out_4));
  LED led_9 (.in(tri_led_driver_3_out_3));
  TNAND_3_input tnand_3_input_2 (.in_1(in_1), .in_2(in_1), .in_3(in_2), .out_4(tnand_3_input_2_out_4));
  LED led_10 (.in(tri_led_driver_4_out_4));
  LED led_11 (.in(tri_led_driver_4_out_2));
  tri_led_driver tri_led_driver_4 (
    .in_1(tnand_3_input_2_out_4), .out_2(tri_led_driver_4_out_2), .out_3(tri_led_driver_4_out_3),
    .out_4(tri_led_driver_4_out_4));
  LED led_12 (.in(tri_led_driver_4_out_3));
  TNAND_3_input tnand_3_input_3 (.in_1(in_2), .in_2(in_2), .in_3(out_3), .out_4(tnand_3_input_3_out_4));
  LED led_13 (.in(tri_led_driver_5_out_4));
  LED led_14 (.in(tri_led_driver_5_out_2));
  LED led_15 (.in(tri_led_driver_5_out_3));
  tri_led_driver tri_led_driver_5 (
    .in_1(tnand_3_input_3_out_4), .out_2(tri_led_driver_5_out_2), .out_3(tri_led_driver_5_out_3),
    .out_4(tri_led_driver_5_out_4));
  TNAND_3_input tnand_3_input_4 (
    .in_1(tnand_3_input_1_out_4), .in_2(tnand_3_input_2_out_4), .in_3(tnand_3_input_3_out_4), .out_4(out_3));
  LED led_16 (.in(tri_led_driver_6_out_4));
  LED led_17 (.in(tri_led_driver_6_out_2));
  LED led_18 (.in(tri_led_driver_6_out_3));
  tri_led_driver tri_led_driver_6 (
    .in_1(out_3), .out_2(tri_led_driver_6_out_2), .out_3(tri_led_driver_6_out_3),
    .out_4(tri_led_driver_6_out_4));

  // Notes on the sheet:
  //   T0 -1, -1, -1 -- ok
  //   T1 -1, 0, -1 -- ok
  //   T2 -1, 1, -1 -- ok
  //   T3 0, 1, 0 -- BAD!
  //   Usually oscilates if you move it?!
  //   Initializes to unknown state, set both inputs to -1 to initialize
  //   *Almost* works.  Fails when one input moves two states, for example:
  //   If that's the case, B broke the rules here, and the C gate works
  //   Like the RS latch, we can set a rule, you must not advance until gate matches you.
endmodule
